// Logisim project maquina.circ as structural Verilog: 2 circuits, main circuit main
module main (
  input  A,
  input  B,
  input  C,
  input  D,
  input  E,
  input  F,
  input  G,
  input  H
);

  wire and_1_out, and_2_out, and_3_out, button_1_out;

  Button button_1 (.out(button_1_out));
  and and_1 (and_1_out, button_1_out, B);
  and and_2 (and_2_out, button_1_out, A);
  and and_3 (and_3_out, button_1_out, C);
  // AND_Gate and_4 has open pins: in0=button_1_out, in1=D, out=open
  Deco_custom deco_custom_1 (
    .in_1(and_3_out), .in_2(and_1_out), .in_3(and_2_out));  // open: out_4, out_5, out_6, out_7, out_8, out_9, out_10, out_11
  // AND_Gate and_5 has open pins: in0=button_1_out, in1=E, out=open
  // AND_Gate and_6 has open pins: in0=button_1_out, in1=F, out=open
  // AND_Gate and_7 has open pins: in0=button_1_out, in1=G, out=open
  // AND_Gate and_8 has open pins: in0=button_1_out, in1=H, out=open
  _7_Segment_Display u_7_segment_display_1 ();  // open: g, f, a, b, e, d, c, dp

  // Notes on the sheet:
  //   Dec Ops
endmodule

module Deco_custom (
  input  in_1,
  input  in_2,
  input  in_3,
  output out_4,
  output out_5,
  output out_6,
  output out_7,
  output out_8,
  output out_9,
  output out_10,
  output out_11
);

  wire not_1_out, not_2_out, not_3_out;

  not not_1 (not_1_out, in_1);
  not not_2 (not_2_out, in_2);
  not not_3 (not_3_out, in_3);
  and and_1 (out_4, not_3_out, not_2_out, not_1_out);
  and and_2 (out_5, not_3_out, not_2_out, in_1);
  and and_3 (out_6, not_3_out, in_2, not_1_out);
  and and_4 (out_7, not_3_out, in_2, in_1);
  and and_5 (out_8, in_3, not_2_out, not_1_out);
  and and_6 (out_9, in_3, not_2_out, in_1);
  and and_7 (out_10, in_3, in_2, not_1_out);
  and and_8 (out_11, in_3, in_2, in_1);
endmodule
