// Logisim project prueba1.circ as structural Verilog: 1 circuit, main circuit main
module main (
);

  LED led_1 ();  // open: in
  LED led_2 ();  // open: in
  LED led_3 ();  // open: in
  LED led_4 ();  // open: in
endmodule
